# Fritzing sketch WeatherStation (saved by Fritzing 1.0.5)
breadboards: 1

parts:
  M1 = ESP32-S3-DevKitC-1-N8R8-v1 [part_number=ESP32-S3-DevKitC-1-N8R8-v1]
  A1 = ENS160 AHT21  # not connected
  LED1 = RGB LED (com. cathode, rbg) [color="Red (633nm)" current=0.030A package="5 mm [THT]"]  # not connected
  LED2 = LED - 5mm [color="Yellow (595nm)" current=0.030A package="5 mm [THT]"]  # not connected
  R1 = Resistor [tolerance=±5% resistance=330 package="2512 [SMD]"]  # not connected
  R2 = Resistor [tolerance=±5% resistance=330 package="2512 [SMD]"]  # not connected
  R3 = Resistor [tolerance=±5% resistance=330 package="2512 [SMD]"]  # not connected
  R4 = Resistor [tolerance=±5% resistance=330 package="2512 [SMD]"]  # not connected
  WeAct_E-Ink_Display_240x416_3_7_inch1 = WeAct E-Ink Display 240x416 3.7 inch  # not connected
  J1 = Piezo Speaker  # not connected

nets:
  N1: M1.pin_1, M1.pin_2
  N2: M1.pin_22, M1.pin_23, M1.pin_24, M1.pin_44

custom parts:
  ESP32-S3-DevKitC-1-N8R8-v1: ESP32-S3-DevKitC-1-N8R8-v1 This module is 44pins long (2x22) and 11 pins width.
  ENS160 AHT21: The CO2 Gas- Air- Sensor is based on ENS160 in combination with an AHT21 Temperature Humidity Sensor.
